# Fritzing sketch pcb-design (saved by Fritzing 0.8.3b)
circuit board: 8.98561cm x 5.35817cm
breadboards: 1

parts:
  stepper = female pin header, 5 pins [form="♀ (female)"]
  rst = Pushbutton [package="[THT]"]
  shutter = female pin header, 2 pins [form="♀ (female)"]
  power_led = female pin header, 2 pins [form="♀ (female)"]
  servo = female pin header, 3 pins [form="♀ (female)"]
  U2 = Voltage Regulator - 5V [package="TO220 [THT]"]
  C1 = Electrolytic Capacitor [capacitance=10µF voltage=20V package="100 mil [THT, electrolytic]"]
  C2 = Electrolytic Capacitor [capacitance=10µF voltage=20V package="100 mil [THT, electrolytic]"]
  pwr_sw = female pin header, 2 pins [form="♀ (female)"]
  R1 = Resistor [tolerance=±5% resistance=220 package=THT]
  R2 = Resistor [tolerance=±5% resistance=10k package=THT]
  pwr_in = Generic female header - 2 pins [form="♀ (female)" package=THT]
  serial = Generic female header - 4 pins [form="♀ (female)" package=THT]
  C3 = Tantalum Capacitor [capacitance=22µF package="100 mil [THT, tantalum]"]
  C4 = Tantalum Capacitor [capacitance=22µF package="100 mil [THT, tantalum]"]
  R3 = Resistor [tolerance=±5% resistance=2.2k package=THT]
  R4 = Resistor [tolerance=±5% resistance=2.2k package=THT]
  ready_led = female pin header, 2 pins [form="♀ (female)"]
  R5 = Resistor [tolerance=±5% resistance=220 package=THT]
  status_led = female pin header, 2 pins [form="♀ (female)"]
  R6 = Resistor [tolerance=±5% resistance=220 package=THT]
  l_meter = Generic female header - 3 pins [form="♀ (female)" package=THT]
  rst_cntr = Pushbutton [package="[THT]"]
  uln2003 = ULN2003A [package="DIP16 [THT]"]
  XTAL2 = Crystal [frequency="16 MHz" package=THT]
  atmega = atmega168 [package=dip]

nets:
  VCC: stepper.pin1, shutter.pin2, servo.pin2, U2.output_voltage, C1.+, C2.+, R1.Pin_0, R2.Pin_0, serial.+5v, l_meter.vcc, rst_cntr.Pin_2, uln2003.COM_-_Common, atmega.VCC, atmega.AVCC, atmega.AREF
  N1: stepper.pin2, uln2003.Out_4
  N2: stepper.pin3, uln2003.Out_3
  N3: stepper.pin4, uln2003.Out_2
  N4: stepper.pin5, uln2003.Out_1
  N5: rst.Pin_1, rst.Pin_2, R2.Pin_1, atmega.RESET
  GND: rst.Pin_3, rst.Pin_4, power_led.pin1, servo.pin3, U2.GND, C1.-, C2.-, pwr_in.ground, serial.gnd, C3.-, C4.-, R3.Pin_0, R4.Pin_0, R5.Pin_0, R6.Pin_0, l_meter.gnd, uln2003.0V, atmega.GND
  N6: shutter.pin1, R4.Pin_1, atmega.D11_(PWM)
  N7: power_led.pin2, R1.Pin_1
  N8: servo.pin1, atmega.D3_(PWM)
  N9: U2.input_voltage, pwr_sw.pin1
  N10: pwr_sw.pin2, pwr_in.vcc
  N11: serial.tx, atmega.D0_(RX)
  N12: serial.rx, atmega.D1_(TX)
  N13: C3.+, XTAL2.pin_1, atmega.XLAT1
  N14: C4.+, XTAL2.pin_0, atmega.XLAT2
  N15: R3.Pin_1, rst_cntr.Pin_3, rst_cntr.Pin_4, atmega.D9_(PWM)
  N16: ready_led.pin1, atmega.D12
  N17: ready_led.pin2, R5.Pin_1
  N18: status_led.pin1, atmega.D13
  N19: status_led.pin2, R6.Pin_1
  N20: l_meter.sig, atmega.A0
  N21: uln2003.In_1, atmega.D5_(PWM)
  N22: uln2003.In_2, atmega.D6_(PWM)
  N23: uln2003.In_3, atmega.D7
  N24: uln2003.In_4, atmega.D8

notes:
  arduino
  pinhole

custom parts:
  Generic female header - 2 pins: Generic female header
  Generic female header - 4 pins: Generic female header
  Generic female header - 3 pins: Generic female header
